// Logisim project exs1.circ as structural Verilog: 1 circuit, main circuit main
module main (
  input  A,
  input  A_2,
  input  B,
  input  B_2,
  input  C,
  input  C_2,
  input  D,
  input  D_2,
  input  E,
  input  E_2,
  input  F
);

  wire and_1_out, and_2_out, and_3_out, and_4_out, and_5_out, or_1_out, or_2_out;

  and and_1 (and_1_out, A, B_2, C);
  and and_2 (and_2_out, D_2, E_2);
  or or_1 (or_1_out, and_1_out, and_2_out);
  LED S (.in(or_1_out));
  and and_3 (and_3_out, A_2, B);
  and and_4 (and_4_out, C_2, D);
  and and_5 (and_5_out, E, F);
  or or_2 (or_2_out, and_3_out, and_4_out, and_5_out);
  LED led_1 (.in(or_2_out));

  // Notes on the sheet:
  //   S = (ABC) + (DE)
  //   S
  //   S
  //   S = (AB) + (CD) + (EF)
endmodule
