// Logisim project exs.circ as structural Verilog: 1 circuit, main circuit main
module main (
  input  A,
  input  A_2,
  input  B,
  input  B_2,
  input  C,
  input  D,
  input  C_2,
  input  A_3,
  input  D_2,
  input  B_3,
  input  C_3,
  input  E,
  input  D_3,
  input  A_4,
  input  F,
  input  B_4,
  input  C_4,
  input  D_4
);

  wire and_1_out, and_2_out, and_3_out, and_4_out, and_5_out, not_1_out, not_2_out, not_3_out, not_4_out,
       not_5_out, not_6_out, or_1_out, or_2_out, or_3_out;

  and and_1 (and_1_out, A, C_2);
  or or_1 (or_1_out, B_2, D_2);
  and and_2 (and_2_out, E, F);
  LED led_1 (.in(or_2_out));
  or or_2 (or_2_out, and_1_out, or_1_out, and_2_out);
  not not_1 (not_1_out, A_2);
  not not_2 (not_2_out, B);
  not not_3 (not_3_out, B_3);
  not not_4 (not_4_out, C_3);
  not not_5 (not_5_out, D_3);
  not not_6 (not_6_out, B_4);
  and and_3 (and_3_out, not_1_out, not_2_out, C, D);
  and and_4 (and_4_out, A_3, not_3_out, not_4_out, not_5_out);
  and and_5 (and_5_out, A_4, not_6_out, C_4, D_4);
  or or_3 (or_3_out, and_3_out, and_4_out, and_5_out);
  LED led_2 (.in(or_3_out));
endmodule
